# Fritzing sketch Sketch (saved by Fritzing 0.9.3b)
circuit board: 8.46667cm x 5.64444cm
breadboards: 1

parts:
  U1 = NodeMCU V1.0
  DHT1 = DHT11 Humitidy and Temperature Sensor
  Деталь1 = Adafruit TSL2561 [part_number="Adafruit #439"]
  R1 = Resistor [tolerance=±10% resistance=1k package=THT]
  R2 = Resistor [tolerance=±5% resistance=47 package=THT]
  LED1 = LEDs [package=led10mm]

nets:
  N1: U1.D0, R1.Pin_1
  N2: U1.D1, Деталь1.SCL
  N3: U1.D2, Деталь1.SDA
  N4: U1.D3, DHT1.NULL
  3V3: U1.3V3, DHT1.VDD, Деталь1.VIN, R2.Pin_1
  GND: U1.GND, DHT1.GND, Деталь1.GND
  N5: U1.D5, LED1.C
  N6: U1.RST, R1.Pin_0
  N7: R2.Pin_0, LED1.A

custom parts:
  NodeMCU V1.0: ESP8266 based NodeMCU
  DHT11 Humitidy and Temperature Sensor: DHT11 Humidity and Temperature Sensor
  Adafruit TSL2561: The TSL2561 luminosity sensor is an advanced digital light sensor, ideal for use in a wide range of light situations. Compared to low cost CdS cells, this sensor is more precise, allowing for exact lux calculations and can be configured for different gain/timing ranges to detect light ranges from up to 0.1 - 40,000+ Lux on the fly. The best part of this sensor is that it contains both infrared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
